# Fritzing sketch AutoCAR (saved by Fritzing 0.9.3b)

parts:
  WeMos_D1_R1 = WeMos D1 R2
  LEFT = hc-sr04
  BACK = hc-sr04
  FRONT = hc-sr04
  RIGHT = hc-sr04

nets:
  N1: WeMos_D1_R1.D2, RIGHT.Echo
  N2: WeMos_D1_R1.D3, RIGHT.Trig
  N3: WeMos_D1_R1.D4, FRONT.Echo
  N4: WeMos_D1_R1.(D5), FRONT.Trig
  N5: WeMos_D1_R1.(D6), BACK.Echo
  N6: WeMos_D1_R1.(D7), BACK.Trig
  N7: WeMos_D1_R1.D8, LEFT.Echo
  N8: WeMos_D1_R1.D9, LEFT.Trig
  GND: WeMos_D1_R1.GND, LEFT.GND, BACK.GND, FRONT.GND, RIGHT.GND
  VCC: WeMos_D1_R1.5V, LEFT.VCC, BACK.VCC, FRONT.VCC, RIGHT.VCC

custom parts:
  WeMos D1 R2: The D1 R2 is a mini wifi board based on the ESP-8266EX.
